# Fritzing sketch SmartAmbientLight (saved by Fritzing 0.9.9b)
breadboards: 1

parts:
  Part1 = Adafruit Trinket M0 [part_number="Adafruit #3500"]
  Part2 = Adafruit LIS3DH [part_number="Adafruit #2809"]
  R1 = PHOTOCELL [package=photocell-kit]
  R2 = Resistor [tolerance=±5% resistance=220 package="2512 [SMD]"]
  Part3 = ws2812b [package="smd 2812b"]

nets:
  N1: Part1.VBAT, Part3.VDD
  GND: Part1.GND, Part2.GND, R2.Pin_0, Part3.VSS
  N2: Part1.D4_A2_PA06_TXD_MOSI, Part3.DIN
  3.3V: Part1.3.3V, Part2.VIN, R1.P$2
  N3: Part1.D2_A1_PA09_SCL_MISO, Part2.SCL
  N4: Part1.D1_A0_PA02, R1.P$1, R2.Pin_1
  N5: Part1.D0_A4_PA08_SDA, Part2.SDA

custom parts:
  Adafruit LIS3DH: The LIS3DH is a very popular low power triple-axis accelerometer. It's low-cost, but has just about every 'extra' you'd want in an accelerometer: Three axis sensing, 10-bit precision ±2g/±4g/±8g/±16g selectable scaling Both I2C (2 possible addresses) and SPI interface options Interrupt output Multiple data rate options 1 Hz to 5Khz As low as 2uA current draw (just the chip itself, not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
